# Fritzing sketch volleycounter_sketch (saved by Fritzing 0.9.0b)
circuit board: 5cm x 5cm
circuit board: 3.2cm x 3.2cm
circuit board: 14cm x 10cm
circuit board: 3.2cm x 3.2cm
breadboards: 1

parts:
  ATMEGA328 = atmega328 [package=dip]
  1uF = Electrolytic Capacitor [capacitance=1µF package="100 mil [THT, electrolytic]"]
  10k = Resistor [tolerance=±5% resistance=10k package=THT]
  LM386 = LM386 [package=dip08]
  180pF = Capacitor [package=cap-pth-small2]
  Flash = female pin header, 6 pins [form="♀ (female)"]
  100uF = Electrolytic Capacitor [capacitance=1µF package="100 mil [THT, electrolytic]"]
  10uF = Electrolytic Capacitor [capacitance=10µF package="100 mil [THT, electrolytic]"]
  10uF_2 = Electrolytic Capacitor [capacitance=1µF package="100 mil [THT, electrolytic]"]
  100uF_2 = Electrolytic Capacitor [capacitance=1µF package="100 mil [THT, electrolytic]"]
  1_5k = Resistor [tolerance=±5% resistance=1.5k package=THT]
  10 = Resistor [tolerance=±5% resistance=1.5k package=THT]
  180pF_2 = Capacitor [package=cap-pth-small2]
  WTV020SD = IC, DIP package, 16 pins [chip_label=WTV020SD]
  B29 = Diode [package=diode-1n4148]
  D1 = Diode [package=diode-1n4148]
  matrix_1 = matrix input [form="♀ (female)" package=THT]
  matrix_din1 = matrix input [form="♀ (female)" package=THT]
  matrix2 = matrix input [form="♀ (female)" package=THT]
  matrix_din3 = matrix input [form="♀ (female)" package=THT]
  RF_Receiver_(5V_DATA_DATA_GND) = RF Receiver [form="♀ (female)" package=THT]
  LED = LED - 5mm [color="Red (633nm)" package="5 mm [THT]"]
  LED2 = LED - 5mm [color="Red (633nm)" package="5 mm [THT]"]
  220 = Resistor [tolerance=±5% resistance=220 package=THT]
  16MHz = Crystal [frequency="16 Mhz" package=THT]
  C1 = Ceramic Capacitor [capacitance="100 nF" package="100 mil [THT, multilayer]"]
  22pF = Ceramic Capacitor [capacitance="100 nF" package="100 mil [THT, multilayer]"]
  220_2 = Resistor [tolerance=±5% resistance=220 package=THT]
  +_-_(6V-9V) = Battery block 9V
  7805 = Voltage Regulator [package=to-220-alt]
  100k = Trimmer Potentiometer [maximum_resistance=10kΩ package=THT]
  Pad44 = Pad [width=1.70418172584795 height=3.09056916070175 connect=center]
  Spk+ = female pin header, 4 pins [form="♀ (female)"]
  Spk- = female pin header, 5 pins [form="♀ (female)"]
  +_- = Battery block 9V
  10uF_3 = Electrolytic Capacitor [capacitance=1µF package="100 mil [THT, electrolytic]"]

nets:
  N1: ATMEGA328.RESET, 1uF.+, 10k.Pin_1
  N2: ATMEGA328.D0_(RX), Flash.pin4
  N3: ATMEGA328.D1_(TX), Flash.pin5
  N4: ATMEGA328.D2, WTV020SD.pin1
  N5: ATMEGA328.D3_(PWM), RF_Receiver_(5V_DATA_DATA_GND).Data
  N6: ATMEGA328.D4, 220_2.Pin_0
  VCC: ATMEGA328.VCC, ATMEGA328.AVCC, 10k.Pin_0, D1.A, matrix_1.VCC
  GND: ATMEGA328.GND
  N7: ATMEGA328.XLAT1, 16MHz.pin_1, 22pF.1
  N8: ATMEGA328.XLAT2, 16MHz.pin_0, C1.0
  N9: ATMEGA328.D5_(PWM), 220.Pin_0
  N10: ATMEGA328.D6_(PWM), matrix_1.DIN
  N11: ATMEGA328.D7, matrix_1.CLK
  N12: ATMEGA328.D8, matrix_1.CS
  N13: ATMEGA328.A2, WTV020SD.pin7
  N14: ATMEGA328.A4, WTV020SD.pin10
  N15: ATMEGA328.A5, WTV020SD.pin15
  N16: 1uF.-, Flash.pin6
  N17: LM386.GAIN, 1_5k.Pin_0, 1_5k.Pin_1
  GND_2: LM386.-IN, LM386.V-, Flash.pin1, 10uF.-, 10.Pin_1, RF_Receiver_(5V_DATA_DATA_GND).GND, +_-_(6V-9V).-, 7805.GND, Spk-.pin1, Spk-.pin3, Spk-.pin5, +_-.-, 10uF_3.-
  N18: LM386.+IN, 100uF.-
  N19: LM386.OUT, 100uF_2.+, 180pF_2.1
  N20: LM386.V+, 10uF.+, +_-_(6V-9V).+, 7805.IN, +_-.+
  N21: LM386.BP, 10uF_2.+
  N22: 180pF.1, 100k.leg2
  N23: 180pF.2, WTV020SD.pin2
  N24: 100uF.+, 100k.wiper
  N25: 10uF_2.-, 100k.leg1, Pad44.pad
  N26: 100uF_2.-, Spk+.pin1, Spk+.pin2, Spk+.pin4
  N27: 10.Pin_0, 180pF_2.2
  N28: WTV020SD.pin16, B29.C
  N29: B29.A, D1.C
  GND_3: matrix_1.GND, matrix_din1.GND, matrix2.GND, matrix_din3.GND, LED.cathode, LED2.cathode, C1.1, 22pF.0
  N30: matrix_din1.CLK, matrix2.CLK
  N31: matrix_din1.CS, matrix2.CS
  N32: matrix_din1.DIN, matrix2.DIN
  VCC_2: matrix_din1.VCC, matrix2.VCC
  VCC_3: matrix_din3.VCC, RF_Receiver_(5V_DATA_DATA_GND).VCC
  N33: LED.anode, 220.Pin_1
  N34: LED2.anode, 220_2.Pin_1
  N35: 7805.OUT, 10uF_3.+

notes:
  DTS  TX  RX  -   -  GND
  Unten
  Marcel
  Imig

custom parts:
  RF Receiver: 433 receiver
